# Fritzing sketch display (saved by Fritzing 0.9.5d)
circuit board: 7.20888cm x 3.96737cm

parts:
  A1 = Wemos S2 Mini [part_number="WeMos D1 Mini Lite"]
  TP1 = TP4056 [chip_label=TP4056 package="DIP (Dual Inline) [THT]"]
  A2 = lcd color display 1.3in 240x240 7pin interface [package=THT]

nets:
  N1: A1.Pin_8, A1.Pin_16, A2.VCC, A2.BLK
  N2: A1.Pin_17, TP1.pin3
  N3: A1.Pin_18, A1.Pin_26, TP1.pin6, A2.GND
  N4: A1.Pin_19, A2.DC
  N5: A1.Pin_20, A2.RES
  N6: A1.Pin_21, A2.SDA
  N7: A1.Pin_22, A2.SCL

custom parts:
  Wemos S2 Mini: A mini wifi board based on the ESP32-S2FN4R2.
  TP4056: A DIP stand-in part for whatever IC you want. With 6 pins on a 300mil dual inline package (DIP) footprint.
  lcd color display 1.3in 240x240 7pin interface: 1.3 Inch Color 240 x 240 IPS TFT LCD Display Screen Module Board 7 Pin 4 Wire ST7789VW Drive IC SPI interface.
